# Fritzing sketch components (saved by Fritzing 0.9.3b)
breadboards: 1

parts:
  WeMos_D1_Mini2 = WeMos D1 Mini
  Temp_Sensor = BME280 Breakout
  CO2_Sensor = MH-Z19 CO2 sensor [part_number=MH-Z19]
  Display = OLED 128x64 I2C Monochrome Display
  Warning_led = ws2812b [package="smd 2812b"]
  PIR = RCWL-0516 Microwave Radar Motion Sensor Module
  D1 = Rectifier Diode [part_number=1N4001 package="Melf DO-213 AB [SMD]"]

nets:
  3V3: WeMos_D1_Mini2.3V3, Temp_Sensor.3.3V, Display.VDD
  VIN: WeMos_D1_Mini2.5V, CO2_Sensor.Vin, PIR.VIN, D1.anode
  N1: WeMos_D1_Mini2.D0, PIR.OUT
  N2: WeMos_D1_Mini2.D1, Temp_Sensor.SCK/SCL
  N3: WeMos_D1_Mini2.D2, Temp_Sensor.SDI/SDA
  N4: WeMos_D1_Mini2.D5, CO2_Sensor.TX
  N5: WeMos_D1_Mini2.D8, CO2_Sensor.RX
  GND: WeMos_D1_Mini2.G, Temp_Sensor.GND, CO2_Sensor.GND, Display.GND, Warning_led.VSS, PIR.GND

notes:
  not supported yet, reserved for future

custom parts:
  RCWL-0516 Microwave Radar Motion Sensor Module: The RCWL-0516 is a microwave radar motion sensor module. Input voltage is 4V to 28V. The 3V3 pin is a power output.
